# Fritzing sketch circuit diagram (saved by Fritzing 1.0.3b)
breadboards: 1

parts:
  Q1 = npn-Powertransistor [package="TO220 [THT]"]
  Q2 = npn-Powertransistor [package="TO220 [THT]"]
  S1 = Momentary Switch [package=ksa_sealed_tac_switch]
  S2 = Momentary Switch [package=ksa_sealed_tac_switch]
  R1 = Resistor [tolerance=±5% power=0.25W resistance=220 package=THT]
  Q3 = NPN-Transistor [package="TO92 [THT]"]
  R2 = Resistor [tolerance=±5% power=0.25W resistance=220 package=THT]
  M1 = DC Motor [voltage_(max)=6V voltage_(min)=3V]

nets:
  N1: Q1.base, Q3.C, R2.Pin_0
  N2: Q1.collector, Q2.emitter
  N3: Q1.emitter, Q3.E
  N4: Q2.base, S1.2
  N5: Q2.collector, M1.pin_1
  N6: S1.4, S2.4, R2.Pin_1, M1.pin_2
  N7: S2.2, R1.Pin_0
  N8: R1.Pin_1, Q3.B
